// Logisim project joystick.circ as structural Verilog: 6 circuits, main circuit main
module main (
);

  wire [2:0] joystick_1_x, joystick_1_y;
  wire [6:0] joystick_2_led_raw_1, joystick_2_led_raw_2, joystick_2_led_raw_3, joystick_2_led_raw_4,
       joystick_2_led_raw_5, joystick_2_led_raw_6, joystick_2_led_raw_7;

  // Probe on joystick_1_x
  Joystick #(.bits(3)) joystick_1 (.x(joystick_1_x), .y(joystick_1_y));
  // Probe on joystick_1_y
  JOYSTICK joystick_2 (
    .Horizontal_position(joystick_1_x), .Vertical_position(joystick_1_y), .LED_raw_1(joystick_2_led_raw_1),
    .LED_raw_2(joystick_2_led_raw_2), .LED_raw_3(joystick_2_led_raw_3), .LED_raw_4(joystick_2_led_raw_4),
    .LED_raw_5(joystick_2_led_raw_5), .LED_raw_6(joystick_2_led_raw_6), .LED_raw_7(joystick_2_led_raw_7));
  DotMatrix #(.inputtype("row"), .matrixcols(7)) dotmatrix_1 (
    .row0(joystick_2_led_raw_1), .row1(joystick_2_led_raw_2), .row2(joystick_2_led_raw_3),
    .row3(joystick_2_led_raw_4), .row4(joystick_2_led_raw_5), .row5(joystick_2_led_raw_6),
    .row6(joystick_2_led_raw_7));
endmodule

// SB
module SIGNAL_BLOCKER (
  input  [6:0] VALUE,
  input  POS0,
  input  POS1,
  input  POS2,
  output [6:0] OUTPUT
);

  wire and_1_out, BLOCK;

  and and_1 (and_1_out, POS0, POS1);
  and and_2 (BLOCK, and_1_out, POS2);
  and and_3 (OUTPUT[6], VALUE[0], BLOCK);
  and and_4 (OUTPUT[5], VALUE[1], BLOCK);
  and and_5 (OUTPUT[4], VALUE[2], BLOCK);
  and and_6 (OUTPUT[3], VALUE[3], BLOCK);
  and and_7 (OUTPUT[2], VALUE[4], BLOCK);
  and and_8 (OUTPUT[1], VALUE[5], BLOCK);
  and and_9 (OUTPUT[0], VALUE[6], BLOCK);
endmodule

module DIRECTOR (
  input  [6:0] HORIZONTAL_POINT,
  input  [2:0] Vertical_Pos,
  output [6:0] LED_raw_1,
  output [6:0] LED_raw_2,
  output [6:0] LED_raw_3,
  output [6:0] LED_raw_4,
  output [6:0] LED_raw_5,
  output [6:0] LED_raw_6,
  output [6:0] LED_raw_7
);

  wire not_1_out, not_2_out, not_3_out, not_4_out, not_5_out, not_6_out, not_7_out, not_8_out, not_9_out;

  not not_1 (not_1_out, Vertical_Pos[2]);
  not not_2 (not_2_out, Vertical_Pos[0]);
  not not_3 (not_3_out, Vertical_Pos[0]);
  not not_4 (not_4_out, Vertical_Pos[1]);
  not not_5 (not_5_out, Vertical_Pos[2]);
  not not_6 (not_6_out, Vertical_Pos[2]);
  not not_7 (not_7_out, Vertical_Pos[1]);
  not not_8 (not_8_out, Vertical_Pos[1]);
  not not_9 (not_9_out, Vertical_Pos[0]);
  SIGNAL_BLOCKER signal_blocker_1 (
    .VALUE(HORIZONTAL_POINT), .POS0(Vertical_Pos[0]), .POS1(not_4_out), .POS2(not_1_out), .OUTPUT(LED_raw_1));
  SIGNAL_BLOCKER signal_blocker_2 (
    .VALUE(HORIZONTAL_POINT), .POS0(not_2_out), .POS1(Vertical_Pos[1]), .POS2(not_5_out), .OUTPUT(LED_raw_2));
  SIGNAL_BLOCKER signal_blocker_3 (
    .VALUE(HORIZONTAL_POINT), .POS0(Vertical_Pos[0]), .POS1(Vertical_Pos[1]), .POS2(not_6_out),
    .OUTPUT(LED_raw_3));
  SIGNAL_BLOCKER signal_blocker_4 (
    .VALUE(HORIZONTAL_POINT), .POS0(not_3_out), .POS1(not_7_out), .POS2(Vertical_Pos[2]), .OUTPUT(LED_raw_4));
  SIGNAL_BLOCKER signal_blocker_5 (
    .VALUE(HORIZONTAL_POINT), .POS0(Vertical_Pos[0]), .POS1(not_8_out), .POS2(Vertical_Pos[2]),
    .OUTPUT(LED_raw_5));
  SIGNAL_BLOCKER signal_blocker_6 (
    .VALUE(HORIZONTAL_POINT), .POS0(not_9_out), .POS1(Vertical_Pos[1]), .POS2(Vertical_Pos[2]),
    .OUTPUT(LED_raw_6));
  SIGNAL_BLOCKER signal_blocker_7 (
    .VALUE(HORIZONTAL_POINT), .POS0(Vertical_Pos[0]), .POS1(Vertical_Pos[1]), .POS2(Vertical_Pos[2]),
    .OUTPUT(LED_raw_7));
endmodule

// DECO
module DECODER (
  input  [2:0] HORIZONTAL_POSITION,
  output [6:0] HORIZONTAL_POINT
);

  wire not_1_out, not_2_out, not_3_out, not_4_out, not_5_out, not_6_out;

  not not_1 (not_1_out, HORIZONTAL_POSITION[1]);
  not not_2 (not_2_out, HORIZONTAL_POSITION[0]);
  not not_3 (not_3_out, HORIZONTAL_POSITION[2]);
  not not_4 (not_4_out, HORIZONTAL_POSITION[1]);
  not not_5 (not_5_out, HORIZONTAL_POSITION[1]);
  not not_6 (not_6_out, HORIZONTAL_POSITION[0]);
  and _1 (HORIZONTAL_POINT[0], HORIZONTAL_POSITION[0], not_1_out, not_3_out);
  and _2 (HORIZONTAL_POINT[1], not_2_out, HORIZONTAL_POSITION[1], not_3_out);
  and _3 (HORIZONTAL_POINT[2], HORIZONTAL_POSITION[0], HORIZONTAL_POSITION[1], not_3_out);
  and _4 (HORIZONTAL_POINT[3], not_2_out, not_4_out, HORIZONTAL_POSITION[2]);
  and _5 (HORIZONTAL_POINT[4], HORIZONTAL_POSITION[0], not_5_out, HORIZONTAL_POSITION[2]);
  and _6 (HORIZONTAL_POINT[5], not_6_out, HORIZONTAL_POSITION[1], HORIZONTAL_POSITION[2]);
  and _7 (HORIZONTAL_POINT[6], HORIZONTAL_POSITION[0], HORIZONTAL_POSITION[1], HORIZONTAL_POSITION[2]);
endmodule

module JOYSTICK (
  input  [2:0] Horizontal_position,
  input  [2:0] Vertical_position,
  output [6:0] LED_raw_1,
  output [6:0] LED_raw_2,
  output [6:0] LED_raw_3,
  output [6:0] LED_raw_4,
  output [6:0] LED_raw_5,
  output [6:0] LED_raw_6,
  output [6:0] LED_raw_7
);

  wire [6:0] decoder_1_horizontal_point;

  // Probe on Horizontal_position
  // Probe on decoder_1_horizontal_point
  DECODER decoder_1 (.HORIZONTAL_POSITION(Horizontal_position), .HORIZONTAL_POINT(decoder_1_horizontal_point));
  DIRECTOR director_1 (
    .HORIZONTAL_POINT(decoder_1_horizontal_point), .Vertical_Pos(Vertical_position), .LED_raw_1(LED_raw_1),
    .LED_raw_2(LED_raw_2), .LED_raw_3(LED_raw_3), .LED_raw_4(LED_raw_4), .LED_raw_5(LED_raw_5),
    .LED_raw_6(LED_raw_6), .LED_raw_7(LED_raw_7));
endmodule

module test (
  input  [6:0] HORIZONTAL_POINT,
  input  [2:0] Vertical_Pos
);

  wire not_1_out, not_2_out, not_3_out, not_4_out, not_5_out, not_6_out, not_7_out, not_8_out, not_9_out;
  wire [6:0] signal_blocker_1_output, signal_blocker_2_output, signal_blocker_3_output,
       signal_blocker_4_output, signal_blocker_5_output, signal_blocker_6_output, signal_blocker_7_output;

  not not_1 (not_1_out, Vertical_Pos[2]);
  not not_2 (not_2_out, Vertical_Pos[0]);
  not not_3 (not_3_out, Vertical_Pos[0]);
  not not_4 (not_4_out, Vertical_Pos[1]);
  not not_5 (not_5_out, Vertical_Pos[2]);
  not not_6 (not_6_out, Vertical_Pos[2]);
  not not_7 (not_7_out, Vertical_Pos[1]);
  not not_8 (not_8_out, Vertical_Pos[1]);
  not not_9 (not_9_out, Vertical_Pos[0]);
  SIGNAL_BLOCKER signal_blocker_1 (
    .VALUE(HORIZONTAL_POINT), .POS0(Vertical_Pos[0]), .POS1(not_4_out), .POS2(not_1_out),
    .OUTPUT(signal_blocker_1_output));
  SIGNAL_BLOCKER signal_blocker_2 (
    .VALUE(HORIZONTAL_POINT), .POS0(not_2_out), .POS1(Vertical_Pos[1]), .POS2(not_5_out),
    .OUTPUT(signal_blocker_2_output));
  SIGNAL_BLOCKER signal_blocker_3 (
    .VALUE(HORIZONTAL_POINT), .POS0(Vertical_Pos[0]), .POS1(Vertical_Pos[1]), .POS2(not_6_out),
    .OUTPUT(signal_blocker_3_output));
  SIGNAL_BLOCKER signal_blocker_4 (
    .VALUE(HORIZONTAL_POINT), .POS0(not_3_out), .POS1(not_7_out), .POS2(Vertical_Pos[2]),
    .OUTPUT(signal_blocker_4_output));
  SIGNAL_BLOCKER signal_blocker_5 (
    .VALUE(HORIZONTAL_POINT), .POS0(Vertical_Pos[0]), .POS1(not_8_out), .POS2(Vertical_Pos[2]),
    .OUTPUT(signal_blocker_5_output));
  SIGNAL_BLOCKER signal_blocker_6 (
    .VALUE(HORIZONTAL_POINT), .POS0(not_9_out), .POS1(Vertical_Pos[1]), .POS2(Vertical_Pos[2]),
    .OUTPUT(signal_blocker_6_output));
  SIGNAL_BLOCKER signal_blocker_7 (
    .VALUE(HORIZONTAL_POINT), .POS0(Vertical_Pos[0]), .POS1(Vertical_Pos[1]), .POS2(Vertical_Pos[2]),
    .OUTPUT(signal_blocker_7_output));
  DotMatrix #(.inputtype("row"), .matrixcols(7), .matrixrows(1)) dotmatrix_1 (.row0(signal_blocker_1_output));
  DotMatrix #(.inputtype("row"), .matrixcols(7), .matrixrows(1)) dotmatrix_2 (.row0(signal_blocker_2_output));
  DotMatrix #(.inputtype("row"), .matrixcols(7), .matrixrows(1)) dotmatrix_3 (.row0(signal_blocker_3_output));
  DotMatrix #(.inputtype("row"), .matrixcols(7), .matrixrows(1)) dotmatrix_4 (.row0(signal_blocker_4_output));
  DotMatrix #(.inputtype("row"), .matrixcols(7), .matrixrows(1)) dotmatrix_5 (.row0(signal_blocker_5_output));
  DotMatrix #(.inputtype("row"), .matrixcols(7), .matrixrows(1)) dotmatrix_6 (.row0(signal_blocker_6_output));
  DotMatrix #(.inputtype("row"), .matrixcols(7), .matrixrows(1)) dotmatrix_7 (.row0(signal_blocker_7_output));
endmodule
